# Fritzing sketch tempSensorBoard (saved by Fritzing 0.9.3b)

parts:
  nodeMCU = NodeMCU V3.0
  OLED_SSD1306 = OLED Monochrome 128x32 I2C [part_number=931]
  DHT22 = DHT22 Humidity and Temperature Sensor
  RTouch = Resistor [tolerance=±5% resistance=100k package="0805 [SMD]"]
  PowerBoost_500 = PowerBoost 500 Charger
  TouchPad = TOUCH [package=touch1]
  Battery_3_7v_2000mAh = LIPO-2000mAh [package=lipo-2000]

nets:
  N1: nodeMCU.D1, OLED_SSD1306.SDA
  N2: nodeMCU.D2, OLED_SSD1306.SCL
  GND: nodeMCU.GND, OLED_SSD1306.GND, DHT22.GND, PowerBoost_500.GND
  N3: nodeMCU.D6, DHT22.DATA
  N4: nodeMCU.D7, RTouch.Pin_0
  N5: nodeMCU.D8, RTouch.Pin_1, TouchPad.T1
  3V3: nodeMCU.3V3, OLED_SSD1306.3.3V
  N6: nodeMCU.Vin, PowerBoost_500.5.0V
  N7: PowerBoost_500.GND_BAT_IN, Battery_3_7v_2000mAh.-
  N8: PowerBoost_500.VBAT_IN, Battery_3_7v_2000mAh.+

notes:
  Nodo THINGER.IO con:
  - DHT22
  - oled SSD1306 128x32
  - Touch Sensor
  - Battery Powered
  - nodeMCU controller

custom parts:
  NodeMCU V3.0: ESP8266 based NodeMCU
  OLED Monochrome 128x32 I2C: These displays are small, only about 1" diagonal, but very readable due to the high contrast of an OLED display. This display is made of 128x32 individual white OLED pixels, each one is turned on or off by the controller chip. Because the display makes its own light, no backlight is required. This reduces the power required to run the OLED and is why the display has such high contrast; we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
