# Fritzing sketch NodeMCU_DHT22_Thingsboard (saved by Fritzing 0.9.3b)
breadboards: 1

parts:
  U1 = NodeMCU V1.0
  DHT1 = DHT22 Humidity and Temperature Sensor
  R1 = Resistor [tolerance=±5% resistance=10k package="0402 [SMD]"]
  U2 = LIPO-2000mAh [package=lipo-2000]
  Componente2 = Micro Lipo Charger

nets:
  GND: U1.GND, DHT1.GND, U2.-, Componente2.GND
  N1: U1.D5, DHT1.NULL
  VIN: U1.Vin, DHT1.VDD, R1.Pin_1, U2.+, Componente2.VBAT
  N2: DHT1.DATA, R1.Pin_0

notes:
  ThingsBoard.io Sensor - NodeMCU v1 + DHT22 Sensor
  K. Ramirez - www.kikeramirez.org - 2018

custom parts:
  NodeMCU V1.0: ESP8266 based NodeMCU
  Micro Lipo Charger: Oh so handy, this little lipo charger is so small and easy to use you can keep it on your desk or mount it easily into any project! Simply plug it via any MicroUSB cable into a USB port and a 3.7V/4.2V lithium polymer or lithium ion rechargeable battery into the JST plug on the other end. There are two LEDs - one red and one green. While charging, the red LED is lit. When the battery is fully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
